# Fritzing sketch ESP32-C6 (saved by Fritzing 1.0.6)
breadboards: 1

parts:
  A3 = ESP32-C6 devkit
  Mod1 = L298N DC motor driver
  M1 = DC Motor [voltage_(max)=6V voltage_(min)=3V]
  M2 = DC Motor [voltage_(max)=6V voltage_(min)=3V]
  A4 = GY-NEO6MV2
  GY1 = MPU-6050 Board GY-521 [form="♀ (female)" package=THT]
  INA1 = INA219 DC Current Sensor Breakout
  A5 = tds-sensor-meter-v1.0_1
  M3 = ph-4502c [package=THT]
  U1 = DFRobot SEN0189 [package=THT]
  U2 = Turbidity Sensor Probe [package=THT]
  A6 = Arduino pluggable terminal
  DS1 = DS18B20 1-Wire Temperature Sensor Probe
  S2 = Toggle Switch spst [package=THT]
  U3 = LM2596 step down module
  VCC1 = Battery
  Mod2 = 2S-BMS
  VCC2 = Battery
  C2 = Electrolytic Capacitor [capacitance=100µF voltage=35V package="200 mil [THT, electrolytic]"]

nets:
  GND: A3.Pin_1, A3.Pin_17, A3.Pin_30, Mod1.GND, A4.Tx, GY1.pin2, A5.pin3, M3.pin4, M3.pin5, U1.P1_3, A6.Pin_3, A6.Pin_4, DS1.GND, C2.-
  N1: A3.Pin_2, A4.Vcc#0, GY1.pin1, INA1.VCC, M3.pin6
  N2: A3.Pin_4, GY1.pin4, INA1.SDA
  N3: A3.Pin_5, GY1.pin3, INA1.SCL
  N4: A3.Pin_6, A4.Rx
  N5: A3.Pin_7, A4.Vcc#1
  N6: A3.Pin_8, M3.pin3
  N7: A3.Pin_9, A5.pin1
  N8: A3.Pin_15, A3.Pin_16, A5.pin2, U1.P1_2, A6.Pin_2, A6.Pin_5, DS1.VDD, U3.OUT+, C2.+
  N9: A3.Pin_20, A6.Pin_1, A6.Pin_6, DS1.DQ
  N10: A3.Pin_22, Mod1.IN4
  N11: A3.Pin_23, Mod1.IN3
  N12: A3.Pin_24, Mod1.IN2
  N13: A3.Pin_25, Mod1.IN1
  N14: A3.Pin_29, U1.P1_1
  N15: Mod1.OUT1, M1.pin_2
  N16: Mod1.OUT2, M1.pin_1
  N17: Mod1.12V, INA1.Vin-2, U3.IN+
  N18: Mod1.OUT3, M2.pin_2
  N19: Mod1.OUT4, M2.pin_1
  N20: Mod1.+5V-J1, Mod1.+5V-J2, Mod1.ENA, Mod1.ENB
  N21: INA1.Vin+2, S2.L1
  N22: U1.P2_1, U2.VCC
  N23: U1.P2_2, U2.pin2
  N24: U1.P2_3, U2.pin1
  N25: S2.COM, VCC1.+, Mod2.pin3#3, VCC2.+
  N26: U3.IN-, VCC1.-, Mod2.pin3#2, VCC2.-

custom parts:
  ESP32-C6 devkit: ESP32 / ESP32-C6 WiFi+Bluetooth Internet Of Things Dual Type-C Development Board Core Board ESP32-C6-DevKit.
  L298N DC motor driver: 2x DC motor driver with 78M05 positive voltage regulator (7..35 V) L298N: max 46 V, 2 A Set 5 V Enable jumper to enable 5 V regultor (needed for the L298N) and +5 V output at screw terminal or supply external +5 V at screw terminal Set ENA and/or ENB to +5 V to enable motor permanently or supply ENA and/or ENB with PWM signal IN1 and IN2 set rotation directory for motor A (OUT1/OUT2) IN2 and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
  GY-NEO6MV2: Description: Module GPS , type GY-NEO6MV2, pour arduino et autres micro-contrôleurs. Caractéristiques De type GY-NEO6MV2 Alimentation 3V-5V Avec Flight Control EEPROM MWC Antenne large céramique, fort signal, 25 x 25 mm Paramètres de configuration sauvegardés en EEPROM Avec batterie de backup de données LED témoin de signal Module miniaturisé 25 x 35 mm Trou de fixation de 3mm Baud rate par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
  MPU-6050 Board GY-521: Acelerometro y Giroscopio MPU-6050 Board GY-521
  INA219 DC Current Sensor Breakout: INA DC Current Sensor Breakout
  : TDS Meter V1.0 Development Board Water Meter Filter Measuring Water Sensor Module.
  ph-4502c: ph-4502c PH Meter.
  DFRobot SEN0189: Turbidity sensor of DFRobot SEN0189
  Turbidity Sensor Probe: Turbidity sensor probe to the DFRobot measure module.
  Arduino pluggable terminal: Arduino pluggable terminal.
  Toggle Switch spst: Toggle Switch single pole single throw
  LM2596 step down module: LM2596 DC-DC step down power supply module 3 A.
  Battery: Your standard 2x 18650 battery pack (7.4 Volts)
  2S-BMS: 2S-BMS LIPO battery charger / protection unit. Note pcb does not match the board as it will likely connect with wires, so pcb is 5 pads suitable for .1in header pins.
